# Fritzing sketch IrieTron 3030 (saved by Fritzing 0.9.3b)

parts:
  Adafruit_nRF52840 = Adafruit Feather nRF52840 [part_number=4062]
  MAX3222 = IC, DIP package, 18 pins [chip_label=IC]
  Data_Jack = 3.5mm Audio Jack [package=audio-jack-3.5mm-smd]
  C1 = Ceramic Capacitor [capacitance="100 nF" package="0805 [SMD, multilayer]"]
  X1 = USB Connectors [package=usb-microb]
  C2 = Ceramic Capacitor [capacitance="100 nF" package="0805 [SMD, multilayer]"]
  C3 = Ceramic Capacitor [capacitance="100 nF" package="0805 [SMD, multilayer]"]
  C4 = Ceramic Capacitor [capacitance="100 nF" package="0805 [SMD, multilayer]"]
  C5 = Ceramic Capacitor [capacitance="100 nF" package="0805 [SMD, multilayer]"]

nets:
  N1: Adafruit_nRF52840.3.3V, MAX3222.pin17, C5.1
  N2: Adafruit_nRF52840.AREF, X1.VBUS
  GND: Adafruit_nRF52840.GND, X1.GND, C3.0, C4.0, C5.0
  N3: Adafruit_nRF52840.RXD, MAX3222.pin13
  N4: Adafruit_nRF52840.TXD, MAX3222.pin12
  N5: MAX3222.pin2, C1.1
  N6: MAX3222.pin3, C3.1
  N7: MAX3222.pin4, C1.0
  N8: MAX3222.pin5, C2.1
  N9: MAX3222.pin6, C2.0
  N10: MAX3222.pin7, C4.1
  N11: MAX3222.pin14, Data_Jack.LEFT
  N12: MAX3222.pin15, Data_Jack.RIGHT
  N13: MAX3222.pin16, Data_Jack.SLEEVE

custom parts:
  Adafruit Feather nRF52840: The Adafruit Feather nRF52840 Express is our take on an 'all-in-one' Arduino-compatible + Bluetooth Low Energy with built in USB plus battery charging, 1 MB of FLASH and 256KB of SRAM. With native USB it's even ready to join the CircuitPython party. For this chip, we've added Arduino IDE support - you can program the nRF52840 chip directly to take full advantage of the Cortex-M4 processor, and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
